// Logisim project Bonus.circ as structural Verilog: 1 circuit, main circuit main
module main (
  input  x,
  input  x_2,
  input  y,
  input  y_2,
  output f,
  output f_2
);

  wire n7408_1_pin2, n7408_1_pin3, n7408_1_pin10, n7408_1_pin11, n7408_2_pin2, n7408_2_pin3, n7408_2_pin10,
       n7408_2_pin11;

  _7408 #(.ShowInternalStructure("true")) u_7408_1 (
    .pin1(x), .pin2(n7408_1_pin2), .pin3(n7408_1_pin3), .pin13(y), .pin12(n7408_1_pin2),
    .pin11(n7408_1_pin11), .pin10(n7408_1_pin10), .pin9(n7408_1_pin10), .pin8(f));  // open: pin4, pin5, pin6
  _7400 #(.ShowInternalStructure("true")) u_7400_1 (
    .pin1(x), .pin2(y), .pin3(n7408_1_pin2), .pin10(n7408_1_pin11), .pin9(n7408_1_pin3), .pin8(n7408_1_pin10));  // open: pin4, pin5, pin6, pin13, pin12, pin11
  _7408 u_7408_2 (
    .pin1(x_2), .pin2(n7408_2_pin2), .pin3(n7408_2_pin3), .pin13(y_2), .pin12(n7408_2_pin2),
    .pin11(n7408_2_pin11), .pin10(n7408_2_pin10), .pin9(n7408_2_pin10), .pin8(f_2));  // open: pin4, pin5, pin6
  _7400 u_7400_2 (
    .pin1(x_2), .pin2(y_2), .pin3(n7408_2_pin2), .pin10(n7408_2_pin11), .pin9(n7408_2_pin3),
    .pin8(n7408_2_pin10));  // open: pin4, pin5, pin6, pin13, pin12, pin11
endmodule
