// Logisim project Main.circ as structural Verilog: 1 circuit, main circuit main
module main (
  input  X,
  input  y,
  output f
);

  wire and_1_out, and_2_out, nand_1_out, nand_2_out;

  nand nand_1 (nand_1_out, X, y);
  and and_1 (and_1_out, X, nand_1_out);
  and and_2 (and_2_out, nand_1_out, y);
  nand nand_2 (nand_2_out, and_1_out, and_2_out);
  and and_3 (f, nand_2_out, nand_2_out);
endmodule
